# Fritzing sketch EEG Circuit (saved by Fritzing 0.9.1b)
breadboards: 1

parts:
  IC4 = IC, DIP package, 8 pins [chip_label=AD620]
  R16 = Resistor [tolerance=±5% resistance=560 package=THT]
  IC5 = OP482 - Low Power, High Speed JFET Quad Operational Amplifier [part_number=TL084]
  IC6 = OP482 - Low Power, High Speed JFET Quad Operational Amplifier [part_number=TL084]
  R17 = Resistor [tolerance=±5% resistance=22k package=THT]
  C12 = Ceramic Capacitor [capacitance=220nF package="100 mil [THT, multilayer]"]
  C13 = Electrolytic Capacitor [capacitance=10µF package="100 mil [THT, electrolytic]"]
  R18 = Resistor [tolerance=±5% resistance=220 package=THT]
  R19 = Resistor [tolerance=±5% resistance=12 package=THT]
  C14 = Ceramic Capacitor [capacitance=220nF package="100 mil [THT, multilayer]"]
  C15 = Ceramic Capacitor [capacitance=220nF package="100 mil [THT, multilayer]"]
  C16 = Ceramic Capacitor [capacitance=220nF package="100 mil [THT, multilayer]"]
  R20 = Resistor [tolerance=±5% resistance=220 package=THT]
  R21 = Resistor [tolerance=±5% resistance=180k package=THT]
  R22 = Resistor [tolerance=±5% resistance=180k package=THT]
  R23 = Resistor [tolerance=±5% resistance=180k package=THT]
  C17 = Ceramic Capacitor [capacitance=100nF package="100 mil [THT, multilayer]"]
  C18 = Ceramic Capacitor [capacitance=25nF package="100 mil [THT, multilayer]"]
  C19 = Electrolytic Capacitor [capacitance=1µF package="100 mil [THT, electrolytic]"]
  R24 = Resistor [tolerance=±5% resistance=1M package=THT]
  C20 = Ceramic Capacitor [capacitance=10nF package="100 mil [THT, multilayer]"]
  R25 = Resistor [tolerance=±5% resistance=100 package=THT]
  R26 = Trimmer Potentiometer [maximum_resistance=2kΩ package=THT]
  R27 = Resistor [tolerance=±5% resistance=220 package=THT]
  R28 = Resistor [tolerance=±5% resistance=22k package=THT]
  Part2 = Arduino Uno (Rev3)
  C21 = Electrolytic Capacitor [capacitance=10µF package="100 mil [THT, electrolytic]"]
  C22 = Ceramic Capacitor [capacitance=220nF package="100 mil [THT, multilayer]"]
  R29 = Resistor [tolerance=±5% resistance=12 package=THT]
  R30 = Resistor [tolerance=±5% resistance=220 package=THT]
  R31 = Resistor [tolerance=±5% resistance=220 package=THT]
  R32 = Resistor [tolerance=±5% resistance=220 package=THT]

nets:
  N1: IC4.pin1, R16.Pin_0
  0V: IC4.pin4, IC5.V-, IC6.V-, Part2.GND, R32.Pin_1
  GND: IC4.pin5, IC5.-INB, IC5.OUTB, IC6.+INB, IC6.+INC, R18.Pin_1, C17.0, R24.Pin_0, R26.leg1, R30.Pin_1
  N2: IC4.pin6, R17.Pin_0
  5V: IC4.pin7, IC5.V+, IC6.V+, Part2.5V, R31.Pin_0
  N3: IC4.pin8, R16.Pin_1
  N4: IC5.OUTA, IC5.-INA, C21.+, R29.Pin_1
  N5: IC5.+INA, C21.-, R30.Pin_0
  N6: IC5.+INB, R31.Pin_1, R32.Pin_0
  N7: IC6.OUTA, IC6.-INA, R19.Pin_1, C14.0
  N8: IC6.+INA, C13.-, R18.Pin_0
  N9: IC6.-INB, C16.1, R20.Pin_1
  N10: IC6.OUTB, C15.1, R20.Pin_0, R22.Pin_0
  N11: IC6.OUTC, R21.Pin_1, C18.1, C19.+
  N12: IC6.-INC, R23.Pin_1, C18.0
  N13: IC6.+IND, C19.-, R24.Pin_1
  N14: IC6.-IND, C20.0, R25.Pin_1, R27.Pin_0
  N15: IC6.OUTD, C20.1, R25.Pin_0, R28.Pin_0
  N16: R17.Pin_1, C12.0
  N17: C12.1, C13.+, R19.Pin_0
  N18: C14.1, C15.0, C16.0
  N19: R21.Pin_0, R22.Pin_1, R23.Pin_0, C17.1
  N20: R26.wiper, R27.Pin_1
  N21: R28.Pin_1, Part2.A0, C22.1
  N22: C22.0, R29.Pin_0

notes:
  EEG Circuit 4, By Alexander Pope, 4
